// Logisim project calc_fin2.0.circ as structural Verilog: 2 circuits, main circuit main
module main (
);

  wire _0, _1, _2, _3, _4, _5, _6, _7, _8, _9, and_1_out, CE, nor_1_out, or_1_out, or_2_out, tunnel,
       tunnel_t, tunnel_t_t, tunnel_t_t_t, X;
  wire [3:0] bin_dec_decoder_1_e0, DATA, register_1_q, register_2_q, register_3_q, register_4_q,
       register_5_q, register_6_q, register_7_q, register_8_q, register_9_q, register_10_q, SELECTOR,
       shift_register_1_q0, shift_register_1_q1, shift_register_1_q2, shift_register_1_q3;

  Register #(.width(4)) register_1 (.D(4'b0010), .en(_2), .Q(register_1_q), .clk(_2));  // open: clr
  Register #(.width(4)) register_2 (.D(4'b0001), .en(_1), .Q(register_2_q), .clk(_1));  // open: clr
  Register #(.width(4)) register_3 (.D(4'b0101), .en(_5), .Q(register_3_q), .clk(_5));  // open: clr
  Register #(.width(4)) register_4 (.D(4'b0000), .en(_0), .Q(register_4_q), .clk(_0));  // open: clr
  Register #(.width(4)) register_5 (.D(4'b0011), .en(_3), .Q(register_5_q), .clk(_3));  // open: clr
  Register #(.width(4)) register_6 (.D(4'b0100), .en(_4), .Q(register_6_q), .clk(_4));  // open: clr
  Multiplexer #(.select(4), .width(4), .enable("false")) multiplexer_1 (
    .in0(register_4_q), .in1(register_2_q), .in2(register_1_q), .in3(register_5_q), .in4(register_6_q),
    .in5(register_3_q), .in6(register_7_q), .in7(register_8_q), .in8(register_9_q), .in9(register_10_q),
    .out(DATA), .sel(SELECTOR));  // open: in10, in11, in12, in13, in14, in15
  bin_dec_decoder bin_dec_decoder_1 (
    .N9(_9), .N8(_8), .N7(_7), .N6(_6), .N5(_5), .N4(_4), .N3(_3), .N2(_2), .N1(_1),
    .E3(bin_dec_decoder_1_e0[3]), .E2(bin_dec_decoder_1_e0[2]), .E1(bin_dec_decoder_1_e0[1]),
    .E0(bin_dec_decoder_1_e0[0]));  // open: N0
  Register #(.width(4)) register_7 (.D(4'b0110), .en(_6), .Q(register_7_q), .clk(_6));  // open: clr
  Register #(.width(4)) register_8 (.D(4'b0111), .en(_7), .Q(register_8_q), .clk(_7));  // open: clr
  Register #(.width(4)) register_9 (.D(4'b1000), .en(_8), .Q(register_9_q), .clk(_8));  // open: clr
  Register #(.width(4)) register_10 (.D(4'b1001), .en(_9), .Q(register_10_q), .clk(_9));  // open: clr
  Register #(.width(4)) register_11 (.D(bin_dec_decoder_1_e0), .en(nor_1_out), .Q(SELECTOR), .clk(nor_1_out), .clr(CE));
  nor nor_1 (nor_1_out, _9, _8, _7, _6, _5, _4, _3, _2, _1, _0);
  Button u__1 (.out(_1));
  Button u__4 (.out(_4));
  Button u__7 (.out(_7));
  Button u__0 (.out(_0));
  Button u__2 (.out(_2));
  Button u__5 (.out(_5));
  Button u__8 (.out(_8));
  Button u_CE (.out(CE));
  Button u__3 (.out(_3));
  Button button (.out(tunnel));
  Button u__6 (.out(_6));
  Button button_2 (.out(tunnel_t));
  Button u_X (.out(X));
  Button u__9 (.out(_9));
  Button button_3 (.out(tunnel_t_t));
  Button button_4 (.out(tunnel_t_t_t));
  or or_1 (or_1_out, _9, _8, _7, _6, _5, _4, _3, _2, _1, _0);
  and and_1 (and_1_out, or_1_out, ~or_2_out);  // AND_Gate
  or or_2 (or_2_out, shift_register_1_q3[0], shift_register_1_q3[1], shift_register_1_q3[2], shift_register_1_q3[3]);
  Hex_Digit_Display hex_digit_display_1 (.value(shift_register_1_q3));  // open: dp
  Hex_Digit_Display hex_digit_display_2 (.value(shift_register_1_q2));  // open: dp
  Shift_Register #(.width(4), .length(4)) shift_register_1 (
    .shift(1'b1), .in(DATA), .clk(and_1_out), .clr(CE), .q0(shift_register_1_q0), .q1(shift_register_1_q1),
    .q2(shift_register_1_q2), .q3(shift_register_1_q3));  // open: out, load, d0, d1, d2, d3
  Hex_Digit_Display hex_digit_display_3 (.value(shift_register_1_q0));  // open: dp
  Hex_Digit_Display hex_digit_display_4 (.value(shift_register_1_q1));  // open: dp
endmodule

module bin_dec_decoder (
  input  N9,
  input  N8,
  input  N7,
  input  N6,
  input  N5,
  input  N4,
  input  N3,
  input  N2,
  input  N1,
  input  N0,
  output E3,
  output E2,
  output E1,
  output E0
);

  or or_1 (E3, N8, N9);
  or or_2 (E2, N4, N5, N6, N7);
  or or_3 (E1, N2, N3, N6, N7);
  or or_4 (E0, N1, N3, N5, N7, N9);
endmodule
