// Logisim project calc_simp.circ as structural Verilog: 6 circuits, main circuit main
module main (
  input  in_1,
  input  in_2,
  input  in_3,
  input  in_4,
  input  Input_1,
  input  in_6,
  input  in_7,
  input  in_8,
  input  in_9,
  input  in_10,
  input  in_11,
  input  in_12,
  input  Input_2,
  input  in_14,
  input  in_15,
  input  in_16,
  input  in_17,
  input  in_18,
  input  x,
  input  in_20,
  output out_21,
  output out_22,
  output out_23,
  output out_24,
  output out_25,
  output out_26,
  output out_27,
  output out_28,
  output out_29,
  output out_30,
  output out_31,
  output out_32,
  output out_33,
  output out_34,
  output out_35,
  output out_36
);

  wire and_2_out, button_out, comparator_1_gt, d_ff_1_qn, neg, ok;
  wire [3:0] A, B, C, D, E, F;
  wire [15:0] adder_1_out, adder_2_out, bit_extender_1_out, bit_extender_2_out, bit_extender_3_out,
       divider_1_out, multiplexer_1_out, multiplexer_2_out, multiplier_1_out, not_1_out, subtractor_1_out;

  Button button (.out(button_out));
  Hex_Digit_Display hex_digit_display_1 (.value(A));  // open: dp
  Hex_Digit_Display hex_digit_display_2 (.value(B));  // open: dp
  BCD bcd_1 (
    .E0(in_9), .E1(in_8), .E2(in_7), .E3(in_6), .E4(Input_1), .E5(in_4), .E6(in_3), .E7(in_2), .UNIT(C),
    .DEC(B), .HUN(A));
  D_Flip_Flop d_ff_1 (.clk(button_out), .D(d_ff_1_qn), .Q(ok), .Qn(d_ff_1_qn));  // open: preset, en, reset
  Hex_Digit_Display hex_digit_display_3 (.value(C));  // open: dp
  assign bit_extender_1_out = {{8{1'b0}}, {in_2, in_3, in_4, Input_1, in_6, in_7, in_8, in_9}};  // Bit_Extender bit_extender_1
  assign bit_extender_2_out = {{15{ok}}, ok};  // Bit_Extender bit_extender_2
  LED led_1 (.in(neg));
  Adder #(.width(16)) adder_1 (.a(bit_extender_3_out), .b(bit_extender_1_out), .out(adder_1_out));  // open: cin, cout
  assign {out_21, out_22, out_23, out_24, out_25, out_26, out_27, out_28, out_29, out_30, out_31, out_32, out_33, out_34, out_35, out_36} = multiplexer_2_out & bit_extender_2_out;  // AND_Gate and_1, 16 bits wide
  Subtractor #(.width(16)) subtractor_1 (
    .a(bit_extender_1_out), .b(bit_extender_3_out), .out(subtractor_1_out));  // open: bin, bout
  Multiplexer #(.select(4), .width(16), .enable("false")) multiplexer_1 (
    .in0({16{1'b0}}), .in1(adder_1_out), .in2(subtractor_1_out), .in3({16{1'b0}}), .in4(multiplier_1_out),
    .in5({16{1'b0}}), .in6({16{1'b0}}), .in7({16{1'b0}}), .in8(divider_1_out), .in9({16{1'b0}}),
    .in10({16{1'b0}}), .in11({16{1'b0}}), .in12({16{1'b0}}), .in13({16{1'b0}}), .in14({16{1'b0}}),
    .in15({16{1'b0}}), .out(multiplexer_1_out), .sel({in_20, x, in_18, in_1}));
  Multiplexer #(.width(16), .enable("false")) multiplexer_2 (
    .in0(multiplexer_1_out), .in1(adder_2_out), .out(multiplexer_2_out), .sel(and_2_out));
  Hex_Digit_Display hex_digit_display_4 (.value(D));  // open: dp
  Multiplier #(.width(16)) multiplier_1 (
    .a(bit_extender_1_out), .b(bit_extender_3_out), .out(multiplier_1_out));  // open: cin, cout
  assign not_1_out = ~multiplexer_1_out;  // NOT_Gate not_1, 16 bits wide
  Adder #(.width(16)) adder_2 (.a(not_1_out), .b(16'h1), .out(adder_2_out));  // open: cin, cout
  Hex_Digit_Display hex_digit_display_5 (.value(E));  // open: dp
  Hex_Digit_Display hex_digit_display_6 (.value(F));  // open: dp
  Divider #(.width(16)) divider_1 (
    .a(bit_extender_1_out), .b(bit_extender_3_out), .out(divider_1_out));  // open: upper, rem
  assign bit_extender_3_out = {{8{1'b0}}, {in_10, in_11, in_12, Input_2, in_14, in_15, in_16, in_17}};  // Bit_Extender bit_extender_3
  Comparator #(.width(16), .mode("unsigned")) comparator_1 (
    .a(bit_extender_3_out), .b(bit_extender_1_out), .gt(comparator_1_gt));  // open: eq, lt
  BCD bcd_2 (
    .E0(in_17), .E1(in_16), .E2(in_15), .E3(in_14), .E4(Input_2), .E5(in_12), .E6(in_11), .E7(in_10),
    .UNIT(F), .DEC(E), .HUN(D));
  and and_2 (and_2_out, in_18, comparator_1_gt);
  and and_3 (neg, ok, and_2_out);

  // Other names for the same wires on the sheet: tunnel = in_1; tunnel_t = in_18; tunnel_t_t = in_20
endmodule

module BCD (
  input  E0,
  input  E1,
  input  E2,
  input  E3,
  input  E4,
  input  E5,
  input  E6,
  input  E7,
  output [3:0] UNIT,
  output [3:0] DEC,
  output [3:0] HUN
);

  wire add3_1_p0, add3_1_p1, add3_1_p2, add3_1_p3, add3_2_p0, add3_2_p1, add3_2_p2, add3_2_p3, add3_3_p0,
       add3_3_p1, add3_3_p2, add3_3_p3, add3_5_p0, add3_5_p1, add3_5_p2, add3_5_p3, add3_7_p0, add3_7_p1,
       add3_7_p2;

  ADD3 add3_1 (.E3(1'b0), .E2(E7), .E1(E6), .E0(E5), .P3(add3_1_p3), .P2(add3_1_p2), .P1(add3_1_p1), .P0(add3_1_p0));
  ADD3 add3_2 (
    .E3(add3_3_p2), .E2(add3_3_p1), .E1(add3_3_p0), .E0(E3), .P3(add3_2_p3), .P2(add3_2_p2), .P1(add3_2_p1),
    .P0(add3_2_p0));
  ADD3 add3_3 (
    .E3(add3_1_p2), .E2(add3_1_p1), .E1(add3_1_p0), .E0(E4), .P3(add3_3_p3), .P2(add3_3_p2), .P1(add3_3_p1),
    .P0(add3_3_p0));
  ADD3 add3_4 (
    .E3(add3_5_p2), .E2(add3_5_p1), .E1(add3_5_p0), .E0(E1), .P3(DEC[0]), .P2(UNIT[3]), .P1(UNIT[2]),
    .P0(UNIT[1]));
  ADD3 add3_5 (
    .E3(add3_2_p2), .E2(add3_2_p1), .E1(add3_2_p0), .E0(E2), .P3(add3_5_p3), .P2(add3_5_p2), .P1(add3_5_p1),
    .P0(add3_5_p0));
  ADD3 add3_6 (
    .E3(add3_7_p2), .E2(add3_7_p1), .E1(add3_7_p0), .E0(add3_5_p3), .P3(HUN[0]), .P2(DEC[3]), .P1(DEC[2]),
    .P0(DEC[1]));
  ADD3 add3_7 (
    .E3(1'b0), .E2(add3_1_p3), .E1(add3_3_p3), .E0(add3_2_p3), .P3(HUN[1]), .P2(add3_7_p2), .P1(add3_7_p1),
    .P0(add3_7_p0));

  assign HUN[3:2] = 2'b00;
  assign UNIT[0] = E0;
endmodule

module ADD3 (
  input  E3,
  input  E2,
  input  E1,
  input  E0,
  output P3,
  output P2,
  output P1,
  output P0
);

  wire and_1_out, and_2_out, and_3_out, and_4_out, and_5_out, and_6_out, and_7_out, and_8_out, and_9_out,
       and_10_out, not_1_out, not_2_out, not_3_out, not_4_out, not_5_out, not_6_out, not_7_out, not_8_out;

  and and_1 (and_1_out, E2, E0);
  and and_2 (and_2_out, E2, E1);
  and and_3 (and_3_out, E2, not_1_out, not_2_out);
  not not_1 (not_1_out, E1);
  not not_2 (not_2_out, E0);
  and and_4 (and_4_out, E3, E0);
  not not_3 (not_3_out, E2);
  and and_5 (and_5_out, not_3_out, E1);
  and and_6 (and_6_out, E1, E0);
  and and_7 (and_7_out, E3, not_4_out);
  not not_4 (not_4_out, E0);
  not not_5 (not_5_out, E3);
  and and_8 (and_8_out, not_5_out, not_6_out, E0);
  not not_6 (not_6_out, E2);
  and and_9 (and_9_out, E2, E1, not_7_out);
  not not_7 (not_7_out, E0);
  and and_10 (and_10_out, E3, not_8_out);
  not not_8 (not_8_out, E0);
  or or_1 (P3, and_1_out, and_2_out, E3);
  or or_2 (P2, and_3_out, and_4_out);
  or or_3 (P1, and_5_out, and_6_out, and_7_out);
  or or_4 (P0, and_8_out, and_9_out, and_10_out);
endmodule

module BCD16 (
  input  E0,
  input  E1,
  input  E2,
  input  E3,
  input  E4,
  input  E5,
  input  E6,
  input  E7,
  input  E8,
  input  E9,
  input  E10,
  input  E11,
  input  E12,
  input  E13,
  input  E14,
  input  E15,
  output [3:0] out_17,
  output [3:0] out_18,
  output [3:0] out_19,
  output [3:0] out_20,
  output [3:0] out_21
);

  wire bcd16_comp2_1_e0, bcd16_comp2_1_e1, bcd16_comp2_1_e2, bcd16_comp2_1_e3, bcd16_comp2_1_e4,
       bcd16_comp2_1_e5, bcd16_comp2_2_e0, bcd16_comp2_2_e1, bcd16_comp2_2_e2, bcd16_comp2_2_e3,
       bcd16_comp2_2_e4, bcd16_comp2_3_e0, bcd16_comp2_3_e1, bcd16_comp2_3_e2, bcd16_comp2_3_e3,
       bcd16_comp2_3_e4, bcd16_comp2_4_e0, bcd16_comp2_4_e1, bcd16_comp2_4_e2, bcd16_comp2_4_e3,
       bcd16_comp2_4_e4, bcd16_comp2_5_e0, bcd16_comp2_5_e1, bcd16_comp2_5_e2, bcd16_comp2_5_e3,
       bcd16_comp2_5_e4, bcd16_comp2_6_e0, bcd16_comp2_6_e1, bcd16_comp2_6_e2, bcd16_comp2_6_e3,
       bcd16_comp2_6_e4, bcd16_comp2_7_e0, bcd16_comp2_7_e1, bcd16_comp2_7_e2, bcd16_comp2_7_e3,
       bcd16_comp2_7_e4, bcd16_comp2_7_e5, bcd16_comp2_8_e4, bcd16_comp2_9_e0, bcd16_comp2_9_e1,
       bcd16_comp2_9_e2, bcd16_comp2_9_e3, bcd16_comp2_9_e4, bcd16_comp2_10_e0, bcd16_comp2_10_e1,
       bcd16_comp2_10_e2, bcd16_comp2_10_e3, bcd16_comp2_10_e4, bcd16_comp2_11_e0, bcd16_comp2_11_e1,
       bcd16_comp2_11_e2, bcd16_comp2_11_e3, bcd16_comp2_11_e4, bcd16_comp2_11_e5, bcd16_comp2_13_e3,
       bcd16_comp2_13_e4, bcd16_comp2_14_e0, bcd16_comp2_14_e1, bcd16_comp2_14_e2, bcd16_comp2_14_e3,
       bcd16_comp2_14_e4, bcd16_comp2_15_e0, bcd16_comp2_15_e1, bcd16_comp2_15_e2;

  BCD16_COMP2 bcd16_comp2_1 (
    .I4(E15), .I3(E14), .I2(E13), .I1(E12), .I0(E11), .E5(bcd16_comp2_1_e5), .E4(bcd16_comp2_1_e4),
    .E3(bcd16_comp2_1_e3), .E2(bcd16_comp2_1_e2), .E1(bcd16_comp2_1_e1), .E0(bcd16_comp2_1_e0));
  BCD16_COMP2 bcd16_comp2_2 (
    .I4(bcd16_comp2_3_e2), .I3(bcd16_comp2_3_e1), .I2(bcd16_comp2_3_e0), .I1(E8), .I0(E7),
    .E4(bcd16_comp2_2_e4), .E3(bcd16_comp2_2_e3), .E2(bcd16_comp2_2_e2), .E1(bcd16_comp2_2_e1),
    .E0(bcd16_comp2_2_e0));  // open: E5
  BCD16_COMP2 bcd16_comp2_3 (
    .I4(bcd16_comp2_1_e2), .I3(bcd16_comp2_1_e1), .I2(bcd16_comp2_1_e0), .I1(E10), .I0(E9),
    .E4(bcd16_comp2_3_e4), .E3(bcd16_comp2_3_e3), .E2(bcd16_comp2_3_e2), .E1(bcd16_comp2_3_e1),
    .E0(bcd16_comp2_3_e0));  // open: E5
  BCD16_COMP2 bcd16_comp2_4 (
    .I4(bcd16_comp2_5_e2), .I3(bcd16_comp2_5_e1), .I2(bcd16_comp2_5_e0), .I1(E4), .I0(E3),
    .E4(bcd16_comp2_4_e4), .E3(bcd16_comp2_4_e3), .E2(bcd16_comp2_4_e2), .E1(bcd16_comp2_4_e1),
    .E0(bcd16_comp2_4_e0));  // open: E5
  BCD16_COMP2 bcd16_comp2_5 (
    .I4(bcd16_comp2_2_e2), .I3(bcd16_comp2_2_e1), .I2(bcd16_comp2_2_e0), .I1(E6), .I0(E5),
    .E4(bcd16_comp2_5_e4), .E3(bcd16_comp2_5_e3), .E2(bcd16_comp2_5_e2), .E1(bcd16_comp2_5_e1),
    .E0(bcd16_comp2_5_e0));  // open: E5
  BCD16_COMP2 bcd16_comp2_6 (
    .I4(bcd16_comp2_7_e2), .I3(bcd16_comp2_7_e1), .I2(bcd16_comp2_7_e0), .I1(bcd16_comp2_2_e4),
    .I0(bcd16_comp2_2_e3), .E4(bcd16_comp2_6_e4), .E3(bcd16_comp2_6_e3), .E2(bcd16_comp2_6_e2),
    .E1(bcd16_comp2_6_e1), .E0(bcd16_comp2_6_e0));  // open: E5
  BCD16_COMP2 bcd16_comp2_7 (
    .I4(bcd16_comp2_1_e5), .I3(bcd16_comp2_1_e4), .I2(bcd16_comp2_1_e3), .I1(bcd16_comp2_3_e4),
    .I0(bcd16_comp2_3_e3), .E5(bcd16_comp2_7_e5), .E4(bcd16_comp2_7_e4), .E3(bcd16_comp2_7_e3),
    .E2(bcd16_comp2_7_e2), .E1(bcd16_comp2_7_e1), .E0(bcd16_comp2_7_e0));
  BCD16_COMP2 bcd16_comp2_8 (
    .I4(bcd16_comp2_4_e2), .I3(bcd16_comp2_4_e1), .I2(bcd16_comp2_4_e0), .I1(E2), .I0(E1),
    .E4(bcd16_comp2_8_e4), .E3(out_18[0]), .E2(out_17[3]), .E1(out_17[2]), .E0(out_17[1]));  // open: E5
  BCD16_COMP2 bcd16_comp2_9 (
    .I4(bcd16_comp2_10_e2), .I3(bcd16_comp2_10_e1), .I2(bcd16_comp2_10_e0), .I1(bcd16_comp2_4_e4),
    .I0(bcd16_comp2_4_e3), .E4(bcd16_comp2_9_e4), .E3(bcd16_comp2_9_e3), .E2(bcd16_comp2_9_e2),
    .E1(bcd16_comp2_9_e1), .E0(bcd16_comp2_9_e0));  // open: E5
  BCD16_COMP2 bcd16_comp2_10 (
    .I4(bcd16_comp2_6_e2), .I3(bcd16_comp2_6_e1), .I2(bcd16_comp2_6_e0), .I1(bcd16_comp2_5_e4),
    .I0(bcd16_comp2_5_e3), .E4(bcd16_comp2_10_e4), .E3(bcd16_comp2_10_e3), .E2(bcd16_comp2_10_e2),
    .E1(bcd16_comp2_10_e1), .E0(bcd16_comp2_10_e0));  // open: E5
  BCD16_COMP2 bcd16_comp2_11 (
    .I4(bcd16_comp2_7_e5), .I3(bcd16_comp2_7_e4), .I2(bcd16_comp2_7_e3), .I1(bcd16_comp2_6_e4),
    .I0(bcd16_comp2_6_e3), .E5(bcd16_comp2_11_e5), .E4(bcd16_comp2_11_e4), .E3(bcd16_comp2_11_e3),
    .E2(bcd16_comp2_11_e2), .E1(bcd16_comp2_11_e1), .E0(bcd16_comp2_11_e0));
  BCD16_COMP2 bcd16_comp2_12 (
    .I4(1'b0), .I3(bcd16_comp2_9_e2), .I2(bcd16_comp2_9_e1), .I1(bcd16_comp2_9_e0), .I0(bcd16_comp2_8_e4),
    .E3(out_19[0]), .E2(out_18[3]), .E1(out_18[2]), .E0(out_18[1]));  // open: E5, E4
  BCD16_COMP2 bcd16_comp2_13 (
    .I4(bcd16_comp2_14_e2), .I3(bcd16_comp2_14_e1), .I2(bcd16_comp2_14_e0), .I1(bcd16_comp2_9_e4),
    .I0(bcd16_comp2_9_e3), .E4(bcd16_comp2_13_e4), .E3(bcd16_comp2_13_e3), .E2(out_19[3]), .E1(out_19[2]),
    .E0(out_19[1]));  // open: E5
  BCD16_COMP2 bcd16_comp2_14 (
    .I4(bcd16_comp2_11_e2), .I3(bcd16_comp2_11_e1), .I2(bcd16_comp2_11_e0), .I1(bcd16_comp2_10_e4),
    .I0(bcd16_comp2_10_e3), .E4(bcd16_comp2_14_e4), .E3(bcd16_comp2_14_e3), .E2(bcd16_comp2_14_e2),
    .E1(bcd16_comp2_14_e1), .E0(bcd16_comp2_14_e0));  // open: E5
  BCD16_COMP2 bcd16_comp2_15 (
    .I4(bcd16_comp2_11_e5), .I3(bcd16_comp2_11_e4), .I2(bcd16_comp2_11_e3), .I1(bcd16_comp2_14_e4),
    .I0(bcd16_comp2_14_e3), .E5(out_21[3]), .E4(out_21[2]), .E3(out_21[1]), .E2(bcd16_comp2_15_e2),
    .E1(bcd16_comp2_15_e1), .E0(bcd16_comp2_15_e0));
  BCD16_COMP2 bcd16_comp2_16 (
    .I4(bcd16_comp2_15_e2), .I3(bcd16_comp2_15_e1), .I2(bcd16_comp2_15_e0), .I1(bcd16_comp2_13_e4),
    .I0(bcd16_comp2_13_e3), .E4(out_21[0]), .E3(out_20[3]), .E2(out_20[2]), .E1(out_20[1]), .E0(out_20[0]));  // open: E5

  assign out_17[0] = E0;
endmodule

module BCD16_COMP (
  input  I4,
  input  I3,
  input  I2,
  input  I1,
  input  I0,
  output E5,
  output E4,
  output E3,
  output E2,
  output E1,
  output E0
);

  wire and_1_out, and_2_out, and_3_out, and_4_out, and_5_out, and_6_out, and_7_out, and_8_out, and_9_out,
       and_10_out, and_11_out, and_12_out, and_13_out, and_14_out, and_15_out, and_16_out, and_17_out,
       and_18_out, and_19_out, and_20_out, and_21_out, and_22_out, and_23_out, and_24_out, and_25_out,
       and_26_out, and_27_out, and_28_out, and_29_out, and_30_out, and_31_out, and_32_out, and_33_out,
       and_34_out, and_35_out, and_36_out, and_37_out, and_38_out, not_1_out, not_2_out, not_3_out,
       not_4_out, not_5_out, not_6_out, not_7_out, not_8_out, not_9_out, not_10_out, not_11_out, not_12_out,
       not_13_out, not_14_out, not_15_out, not_16_out, not_17_out, not_18_out, not_19_out, not_20_out,
       not_21_out, not_22_out, not_23_out, not_24_out, not_25_out, not_26_out, not_27_out, not_28_out,
       not_29_out, not_30_out, not_31_out, not_32_out, not_33_out, not_34_out, not_35_out, not_36_out,
       not_37_out, not_38_out, not_39_out, not_40_out, not_41_out, not_42_out, not_43_out, not_44_out,
       not_45_out, not_46_out, not_47_out, not_48_out, not_49_out, not_50_out, not_51_out, not_52_out,
       not_53_out, not_54_out, not_55_out, not_56_out, not_57_out, not_58_out, not_59_out, not_60_out,
       not_61_out, not_62_out, not_63_out, not_64_out, not_65_out, not_66_out, not_67_out, not_68_out,
       not_69_out, not_70_out, not_71_out, not_72_out, not_73_out;

  and and_1 (and_1_out, I4, I2);
  and and_2 (and_2_out, I4, I3);
  not not_1 (not_1_out, I4);
  not not_2 (not_2_out, I4);
  not not_3 (not_3_out, I3);
  not not_4 (not_4_out, I2);
  not not_5 (not_5_out, I4);
  not not_6 (not_6_out, I3);
  not not_7 (not_7_out, I4);
  not not_8 (not_8_out, I3);
  not not_9 (not_9_out, I4);
  not not_10 (not_10_out, I4);
  not not_11 (not_11_out, I2);
  not not_12 (not_12_out, I1);
  not not_13 (not_13_out, I3);
  not not_14 (not_14_out, I2);
  not not_15 (not_15_out, I2);
  not not_16 (not_16_out, I2);
  not not_17 (not_17_out, I1);
  not not_18 (not_18_out, I4);
  not not_19 (not_19_out, I3);
  not not_20 (not_20_out, I1);
  not not_21 (not_21_out, I0);
  not not_22 (not_22_out, I4);
  not not_23 (not_23_out, I2);
  not not_24 (not_24_out, I1);
  not not_25 (not_25_out, I4);
  not not_26 (not_26_out, I0);
  not not_27 (not_27_out, I3);
  not not_28 (not_28_out, I2);
  not not_29 (not_29_out, I2);
  not not_30 (not_30_out, I1);
  not not_31 (not_31_out, I0);
  not not_32 (not_32_out, I1);
  not not_33 (not_33_out, I3);
  not not_34 (not_34_out, I2);
  not not_35 (not_35_out, I0);
  not not_36 (not_36_out, I4);
  not not_37 (not_37_out, I3);
  not not_38 (not_38_out, I4);
  not not_39 (not_39_out, I1);
  not not_40 (not_40_out, I0);
  not not_41 (not_41_out, I4);
  not not_42 (not_42_out, I1);
  not not_43 (not_43_out, I1);
  not not_44 (not_44_out, I0);
  not not_45 (not_45_out, I3);
  not not_46 (not_46_out, I2);
  not not_47 (not_47_out, I1);
  not not_48 (not_48_out, I3);
  not not_49 (not_49_out, I2);
  not not_50 (not_50_out, I4);
  not not_51 (not_51_out, I3);
  not not_52 (not_52_out, I2);
  not not_53 (not_53_out, I1);
  not not_54 (not_54_out, I4);
  not not_55 (not_55_out, I2);
  not not_56 (not_56_out, I1);
  not not_57 (not_57_out, I0);
  not not_58 (not_58_out, I3);
  not not_59 (not_59_out, I2);
  not not_60 (not_60_out, I1);
  not not_61 (not_61_out, I0);
  not not_62 (not_62_out, I4);
  not not_63 (not_63_out, I2);
  not not_64 (not_64_out, I4);
  not not_65 (not_65_out, I3);
  not not_66 (not_66_out, I0);
  not not_67 (not_67_out, I4);
  not not_68 (not_68_out, I1);
  not not_69 (not_69_out, I2);
  not not_70 (not_70_out, I0);
  not not_71 (not_71_out, I3);
  not not_72 (not_72_out, I1);
  not not_73 (not_73_out, I0);
  or or_1 (E5, and_1_out, and_2_out);
  and and_3 (and_3_out, not_1_out, I3, I1);
  and and_4 (and_4_out, not_2_out, I3, I2);
  and and_5 (and_5_out, I3, I2, I1);
  and and_6 (and_6_out, I4, not_3_out, not_4_out);
  and and_7 (and_7_out, not_5_out, not_6_out, I2, I0);
  and and_8 (and_8_out, not_7_out, not_8_out, I2, I1);
  and and_9 (and_9_out, not_9_out, I2, I1, I0);
  and and_10 (and_10_out, not_10_out, I3, not_11_out, not_12_out);
  and and_11 (and_11_out, I4, not_13_out, not_14_out);
  and and_12 (and_12_out, I4, not_15_out, I0);
  and and_13 (and_13_out, I4, not_16_out, I1);
  and and_14 (and_14_out, I4, I3, I2, not_17_out);
  and and_15 (and_15_out, not_18_out, not_19_out, I2, not_20_out, not_21_out);
  and and_16 (and_16_out, not_22_out, I3, not_23_out, not_24_out, I0);
  and and_17 (and_17_out, not_25_out, I3, I2, I1, not_26_out);
  and and_18 (and_18_out, I4, not_27_out, not_28_out, I1, I0);
  and and_19 (and_19_out, I4, I3, not_29_out, not_30_out, not_31_out);
  and and_20 (and_20_out, I4, I3, I2, not_32_out, I0);
  and and_21 (and_21_out, not_33_out, not_34_out, I1, not_35_out);
  and and_22 (and_22_out, not_36_out, not_37_out, I1, I0);
  and and_23 (and_23_out, not_38_out, I3, not_39_out, not_40_out);
  and and_24 (and_24_out, not_41_out, I3, I2, not_42_out);
  and and_25 (and_25_out, I3, I2, not_43_out, not_44_out);
  and and_26 (and_26_out, I4, not_45_out, not_46_out, not_47_out, I0);
  and and_27 (and_27_out, I4, not_48_out, I2, I1);
  and and_28 (and_28_out, I4, I3, not_49_out, I1, I0);
  and and_29 (and_29_out, not_50_out, not_51_out, not_52_out, not_53_out);
  and and_30 (and_30_out, not_54_out, not_55_out, not_56_out, not_57_out);
  and and_31 (and_31_out, not_58_out, not_59_out, not_60_out, not_61_out);
  and and_32 (and_32_out, not_62_out, not_63_out, I1, I0);
  and and_33 (and_33_out, not_64_out, not_65_out, I2, I1, not_66_out);
  and and_34 (and_34_out, not_67_out, I3, I2, not_68_out, I0);
  and and_35 (and_35_out, I4, not_69_out, I1, not_70_out);
  and and_36 (and_36_out, I4, not_71_out, I2, I0);
  and and_37 (and_37_out, I4, I2, I1, I0);
  and and_38 (and_38_out, I4, I3, I2, not_72_out, not_73_out);
  or or_2 (E4, and_3_out, and_4_out, and_5_out, and_6_out);
  or or_3 (E3, and_7_out, and_8_out, and_9_out, and_10_out, and_11_out, and_12_out, and_13_out, and_14_out);
  or or_4 (E2, and_15_out, and_16_out, and_17_out, and_18_out, and_19_out, and_20_out);
  or or_5 (E1, and_21_out, and_22_out, and_23_out, and_24_out, and_25_out, and_26_out, and_27_out, and_28_out);
  or or_6 (E0, and_29_out, and_30_out, and_31_out, and_32_out, and_33_out, and_34_out, and_35_out, and_36_out, and_37_out, and_38_out);
endmodule

module BCD16_COMP2 (
  input  I4,
  input  I3,
  input  I2,
  input  I1,
  input  I0,
  output E5,
  output E4,
  output E3,
  output E2,
  output E1,
  output E0
);

  wire and_1_out, and_2_out, and_3_out, and_4_out, and_5_out, and_6_out, and_7_out, and_8_out, and_9_out,
       and_10_out, and_11_out, and_12_out, and_13_out, and_14_out, and_15_out, and_16_out, and_17_out,
       and_18_out, and_19_out, and_20_out, and_21_out, and_22_out, and_23_out, and_24_out, and_25_out,
       and_26_out, and_27_out, and_28_out, and_29_out, and_30_out, and_31_out, and_32_out, and_33_out,
       and_34_out, and_35_out, and_36_out, and_37_out, and_38_out, not_1_out, not_2_out, not_3_out,
       not_4_out, not_5_out, not_6_out, not_7_out, not_8_out, not_9_out, not_10_out, not_11_out, not_12_out,
       not_13_out, not_14_out, not_15_out, not_16_out, not_17_out, not_18_out, not_19_out, not_20_out,
       not_21_out, not_22_out, not_23_out, not_24_out, not_25_out, not_26_out, not_27_out, not_28_out,
       not_29_out, not_30_out, not_31_out, not_32_out, not_33_out, not_34_out, not_35_out, not_36_out,
       not_37_out, not_38_out, not_39_out, not_40_out, not_41_out, not_42_out, not_43_out, not_44_out,
       not_45_out, not_46_out, not_47_out, not_48_out, not_49_out, not_50_out, not_51_out, not_52_out,
       not_53_out, not_54_out, not_55_out, not_56_out, not_57_out, not_58_out, not_59_out, not_60_out,
       not_61_out, not_62_out, not_63_out, not_64_out, not_65_out, not_66_out, not_67_out, not_68_out,
       not_69_out, not_70_out, not_71_out;

  and and_1 (and_1_out, I4, I2);
  and and_2 (and_2_out, I4, I3);
  not not_1 (not_1_out, I4);
  not not_2 (not_2_out, I4);
  not not_3 (not_3_out, I3);
  not not_4 (not_4_out, I2);
  not not_5 (not_5_out, I4);
  not not_6 (not_6_out, I3);
  not not_7 (not_7_out, I4);
  not not_8 (not_8_out, I3);
  not not_9 (not_9_out, I4);
  not not_10 (not_10_out, I4);
  not not_11 (not_11_out, I2);
  not not_12 (not_12_out, I1);
  not not_13 (not_13_out, I3);
  not not_14 (not_14_out, I2);
  not not_15 (not_15_out, I2);
  not not_16 (not_16_out, I2);
  not not_17 (not_17_out, I1);
  not not_18 (not_18_out, I4);
  not not_19 (not_19_out, I3);
  not not_20 (not_20_out, I1);
  not not_21 (not_21_out, I0);
  not not_22 (not_22_out, I4);
  not not_23 (not_23_out, I2);
  not not_24 (not_24_out, I1);
  not not_25 (not_25_out, I4);
  not not_26 (not_26_out, I0);
  not not_27 (not_27_out, I3);
  not not_28 (not_28_out, I2);
  not not_29 (not_29_out, I2);
  not not_30 (not_30_out, I1);
  not not_31 (not_31_out, I0);
  not not_32 (not_32_out, I1);
  not not_33 (not_33_out, I3);
  not not_34 (not_34_out, I2);
  not not_35 (not_35_out, I0);
  not not_36 (not_36_out, I4);
  not not_37 (not_37_out, I3);
  not not_38 (not_38_out, I4);
  not not_39 (not_39_out, I1);
  not not_40 (not_40_out, I0);
  not not_41 (not_41_out, I4);
  not not_42 (not_42_out, I1);
  not not_43 (not_43_out, I1);
  not not_44 (not_44_out, I0);
  not not_45 (not_45_out, I3);
  not not_46 (not_46_out, I2);
  not not_47 (not_47_out, I1);
  not not_48 (not_48_out, I3);
  not not_49 (not_49_out, I2);
  not not_50 (not_50_out, I4);
  not not_51 (not_51_out, I3);
  not not_52 (not_52_out, I2);
  not not_53 (not_53_out, I4);
  not not_54 (not_54_out, I2);
  not not_55 (not_55_out, I4);
  not not_56 (not_56_out, I3);
  not not_57 (not_57_out, I0);
  not not_58 (not_58_out, I4);
  not not_59 (not_59_out, I2);
  not not_60 (not_60_out, I1);
  not not_61 (not_61_out, I0);
  not not_62 (not_62_out, I4);
  not not_63 (not_63_out, I1);
  not not_64 (not_64_out, I3);
  not not_65 (not_65_out, I2);
  not not_66 (not_66_out, I0);
  not not_67 (not_67_out, I2);
  not not_68 (not_68_out, I0);
  not not_69 (not_69_out, I3);
  not not_70 (not_70_out, I1);
  not not_71 (not_71_out, I0);
  or or_1 (E5, and_1_out, and_2_out);
  and and_3 (and_3_out, not_1_out, I3, I1);
  and and_4 (and_4_out, not_2_out, I3, I2);
  and and_5 (and_5_out, I3, I2, I1);
  and and_6 (and_6_out, I4, not_3_out, not_4_out);
  and and_7 (and_7_out, not_5_out, not_6_out, I2, I0);
  and and_8 (and_8_out, not_7_out, not_8_out, I2, I1);
  and and_9 (and_9_out, not_9_out, I2, I1, I0);
  and and_10 (and_10_out, not_10_out, I3, not_11_out, not_12_out);
  and and_11 (and_11_out, I4, not_13_out, not_14_out);
  and and_12 (and_12_out, I4, not_15_out, I0);
  and and_13 (and_13_out, I4, not_16_out, I1);
  and and_14 (and_14_out, I4, I3, I2, not_17_out);
  and and_15 (and_15_out, not_18_out, not_19_out, I2, not_20_out, not_21_out);
  and and_16 (and_16_out, not_22_out, I3, not_23_out, not_24_out, I0);
  and and_17 (and_17_out, not_25_out, I3, I2, I1, not_26_out);
  and and_18 (and_18_out, I4, not_27_out, not_28_out, I1, I0);
  and and_19 (and_19_out, I4, I3, not_29_out, not_30_out, not_31_out);
  and and_20 (and_20_out, I4, I3, I2, not_32_out, I0);
  and and_21 (and_21_out, not_33_out, not_34_out, I1, not_35_out);
  and and_22 (and_22_out, not_36_out, not_37_out, I1, I0);
  and and_23 (and_23_out, not_38_out, I3, not_39_out, not_40_out);
  and and_24 (and_24_out, not_41_out, I3, I2, not_42_out);
  and and_25 (and_25_out, I3, I2, not_43_out, not_44_out);
  and and_26 (and_26_out, I4, not_45_out, not_46_out, not_47_out, I0);
  and and_27 (and_27_out, I4, not_48_out, I2, I1);
  and and_28 (and_28_out, I4, I3, not_49_out, I1, I0);
  and and_29 (and_29_out, not_50_out, not_51_out, not_52_out, I0);
  and and_30 (and_30_out, not_53_out, not_54_out, I1, I0);
  and and_31 (and_31_out, not_55_out, not_56_out, I2, I1, not_57_out);
  and and_32 (and_32_out, not_58_out, I3, not_59_out, not_60_out, not_61_out);
  and and_33 (and_33_out, not_62_out, I3, I2, not_63_out, I0);
  and and_34 (and_34_out, I4, not_64_out, not_65_out, not_66_out);
  and and_35 (and_35_out, I4, not_67_out, I1, not_68_out);
  and and_36 (and_36_out, I4, not_69_out, I2, I0);
  and and_37 (and_37_out, I4, I2, I1, I0);
  and and_38 (and_38_out, I4, I3, I2, not_70_out, not_71_out);
  or or_2 (E4, and_3_out, and_4_out, and_5_out, and_6_out);
  or or_3 (E3, and_7_out, and_8_out, and_9_out, and_10_out, and_11_out, and_12_out, and_13_out, and_14_out);
  or or_4 (E2, and_15_out, and_16_out, and_17_out, and_18_out, and_19_out, and_20_out);
  or or_5 (E1, and_21_out, and_22_out, and_23_out, and_24_out, and_25_out, and_26_out, and_27_out, and_28_out);
  or or_6 (E0, and_29_out, and_30_out, and_31_out, and_32_out, and_33_out, and_34_out, and_35_out, and_36_out, and_37_out, and_38_out);
endmodule
